// Logisim project Proc.circ as structural Verilog: 14 circuits, main circuit main
module main (
);

  wire button_1_out;
  wire [15:0] IF_ins, IF_pc_1, IF_pc_2, multiplexer_1_out, reg16_1_out, reg16_2_out, reg16_3_out;

  Button button_1 (.out(button_1_out));
  Multiplexer #(.select(2), .width(16), .enable("false")) multiplexer_1 (
    .in2(IF_pc_1), .in3({16{1'b0}}), .out(multiplexer_1_out), .sel(2'b11));  // open: in0, in1
  reg16 reg16_1 (.IN(multiplexer_1_out), .OUT(reg16_1_out), .CLK(button_1_out));
  IF IF (.PC(reg16_1_out), .INS(IF_ins), .PC_2(IF_pc_2), .PC_1(IF_pc_1));
  reg16 reg16_2 (.IN(IF_ins), .OUT(reg16_2_out), .CLK(button_1_out));
  reg16 reg16_3 (.IN(IF_pc_2), .OUT(reg16_3_out), .CLK(button_1_out));
  ID ID (.PC_in(reg16_3_out), .INS(reg16_2_out));  // open: TGT_sel, WE, PC_out, OP, rT, TGT, SRC1, SRC2, ope0
endmodule

module IF (
  input  [15:0] PC,
  output [15:0] INS,
  output [15:0] PC_2,
  output [15:0] PC_1
);

  ROM #(.addrWidth(16), .dataWidth(16)) rom_1 (.addr(PC), .data(INS), .sel(1'b1));
  Adder #(.width(16)) adder_1 (.a(PC), .b(16'h1), .out(PC_1));  // open: cin, cout

  assign PC_2 = PC;

  // Notes on the sheet:
  //   contents of rom_1 (hex, n*v repeats v):
  //   6401
endmodule

module ID (
  input  [15:0] PC_in,
  input  [15:0] INS,
  input  [2:0] TGT_sel,
  input  [15:0] TGT,
  input  WE,
  output [15:0] PC_out,
  output [2:0] OP,
  output [2:0] rT,
  output [15:0] SRC1,
  output [15:0] SRC2,
  output [15:0] ope0
);

  wire ctl6_1_op0, ctl6_1_s2;
  wire [2:0] multiplexer_1_out;
  wire [15:0] left_shift_6_1_out, sign_ext_7_1_out;

  Sign_Ext_7 sign_ext_7_1 (.in(INS[15:6]), .out(sign_ext_7_1_out));
  Left_shift_6 left_shift_6_1 (.in(INS[15:6]), .out(left_shift_6_1_out));
  CTL7 ctl7_1 (.OP_in(INS[2:0]), .rA(INS[5:3]), .OP_out(OP), .rT(rT));
  CTL6 ctl6_1 (.OP(OP), .s2(ctl6_1_s2), .op0(ctl6_1_op0));
  Multiplexer #(.width(3), .enable("false")) multiplexer_1 (
    .in0(INS[5:3]), .in1(INS[15:13]), .out(multiplexer_1_out), .sel(ctl6_1_s2));
  Multiplexer #(.width(16), .enable("false")) multiplexer_2 (
    .in0(sign_ext_7_1_out), .in1(left_shift_6_1_out), .out(ope0), .sel(ctl6_1_op0));
  RegisterFile registerfile_1 (
    .SRC1_in(INS[8:6]), .WE(WE), .SRC2_in(multiplexer_1_out), .TGT_sel(TGT_sel), .TGT_in(TGT),
    .SRC1_out(SRC1), .SRC2_out(SRC2));

  assign PC_out = PC_in;
endmodule

module RegisterFile (
  input  [2:0] TGT_sel,
  input  [15:0] TGT_in,
  input  [2:0] SRC1_in,
  input  WE,
  input  [2:0] SRC2_in,
  output [15:0] SRC1_out,
  output [15:0] SRC2_out
);

  wire demultiplexer_1_out1, demultiplexer_1_out2, demultiplexer_1_out3, demultiplexer_1_out4,
       demultiplexer_1_out5, demultiplexer_1_out6, demultiplexer_1_out7;
  wire [15:0] demultiplexer_2_out1, demultiplexer_2_out2, demultiplexer_2_out3, demultiplexer_2_out4,
       demultiplexer_2_out5, demultiplexer_2_out6, demultiplexer_2_out7, register_1_q, register_2_q,
       register_3_q, register_4_q, register_5_q, register_6_q, register_7_q, register_8_q;

  Demultiplexer #(.select(3)) demultiplexer_1 (
    .out1(demultiplexer_1_out1), .out2(demultiplexer_1_out2), .out3(demultiplexer_1_out3),
    .out4(demultiplexer_1_out4), .out5(demultiplexer_1_out5), .out6(demultiplexer_1_out6),
    .out7(demultiplexer_1_out7), .in(WE), .sel(TGT_sel));  // open: out0, en
  Register #(.width(16), .trigger("high")) register_1 (.D({16{1'b0}}), .Q(register_1_q));  // open: en, clk, clr
  Demultiplexer #(.select(3), .width(16)) demultiplexer_2 (
    .out1(demultiplexer_2_out1), .out2(demultiplexer_2_out2), .out3(demultiplexer_2_out3),
    .out4(demultiplexer_2_out4), .out5(demultiplexer_2_out5), .out6(demultiplexer_2_out6),
    .out7(demultiplexer_2_out7), .in(TGT_in), .sel(TGT_sel));  // open: out0, en
  Register #(.width(16), .trigger("high")) register_2 (
    .D(demultiplexer_2_out1), .Q(register_2_q), .clk(demultiplexer_1_out1));  // open: en, clr
  Register #(.width(16), .trigger("high")) register_3 (
    .D(demultiplexer_2_out2), .Q(register_3_q), .clk(demultiplexer_1_out2));  // open: en, clr
  Register #(.width(16), .trigger("high")) register_4 (
    .D(demultiplexer_2_out3), .Q(register_4_q), .clk(demultiplexer_1_out3));  // open: en, clr
  Register #(.width(16), .trigger("high")) register_5 (
    .D(demultiplexer_2_out4), .Q(register_5_q), .clk(demultiplexer_1_out4));  // open: en, clr
  Register #(.width(16), .trigger("high")) register_6 (
    .D(demultiplexer_2_out5), .Q(register_6_q), .clk(demultiplexer_1_out5));  // open: en, clr
  Register #(.width(16), .trigger("high")) register_7 (
    .D(demultiplexer_2_out7), .Q(register_7_q), .clk(demultiplexer_1_out7));  // open: en, clr
  Register #(.width(16), .trigger("high")) register_8 (
    .D(demultiplexer_2_out6), .Q(register_8_q), .clk(demultiplexer_1_out6));  // open: en, clr
  Multiplexer #(.select(3), .width(16)) multiplexer_1 (
    .in0(register_1_q), .in1(register_2_q), .in2(register_3_q), .in3(register_4_q), .in4(register_5_q),
    .in5(register_6_q), .in6(register_8_q), .in7(register_7_q), .out(SRC1_out), .sel(SRC1_in));  // open: en
  Multiplexer #(.select(3), .width(16)) multiplexer_2 (
    .in0(register_1_q), .in1(register_2_q), .in2(register_3_q), .in3(register_4_q), .in4(register_5_q),
    .in5(register_6_q), .in6(register_8_q), .in7(register_7_q), .out(SRC2_out), .sel(SRC2_in));  // open: en
endmodule

module CTL7 (
  input  [2:0] OP_in,
  input  [2:0] rA,
  output [2:0] OP_out,
  output [2:0] rT
);

  wire and_1_out, and_2_out, and_3_out, not_1_out;

  and and_1 (and_1_out, OP_in[2], ~OP_in[1], OP_in[0]);  // AND_Gate
  and and_2 (and_2_out, ~and_1_out, ~and_3_out);  // AND_Gate
  assign rT = and_2_out ? rA : 3'bz;  // Controlled_Buffer controlled_buffer_1
  and and_3 (and_3_out, OP_in[0], OP_in[1], ~OP_in[2]);  // AND_Gate
  not not_1 (not_1_out, and_2_out);
  assign rT = not_1_out ? 3'b000 : 3'bz;  // Controlled_Buffer controlled_buffer_2

  assign OP_out = OP_in;
endmodule

module CTL6 (
  input  [2:0] OP,
  output s2,
  output op0
);

  and and_1 (s2, ~OP[0], ~OP[2]);  // AND_Gate
  nand nand_1 (op0, ~OP[0], OP[1], OP[2]);  // NAND_Gate

  // Notes on the sheet:
  //   0 => rA
  //   1 => RC
  //   1 => Left-Shift 6
endmodule

module Left_shift_6 (
  input  [9:0] in,
  output [15:0] out
);


  assign out = {{6{1'b0}}, in};
endmodule

module Sign_Ext_7 (
  input  [9:0] in,
  output [15:0] out
);

  wire not_2_out;
  wire [15:0] adder_1_out, not_1_out;

  assign not_1_out = ~{{10{1'b0}}, in[5:0]};  // NOT_Gate not_1, 16 bits wide
  Adder #(.width(16)) adder_1 (.a(not_1_out), .b(16'h1), .out(adder_1_out));  // open: cin, cout
  assign out = not_2_out ? {{10{1'b0}}, in[5:0]} : 16'bz;  // Controlled_Buffer controlled_buffer_1
  not not_2 (not_2_out, in[6]);
  assign out = in[6] ? adder_1_out : 16'bz;  // Controlled_Buffer controlled_buffer_2
endmodule

module CTL4 (
  input  [2:0] op,
  output [1:0] MUXimm
);

  wire and_1_out, and_2_out;

  and and_1 (and_1_out, op[2], ~op[1]);  // AND_Gate
  and and_2 (and_2_out, ~op[2], op[0]);  // AND_Gate
  and and_3 (MUXimm[1], op[0], op[1], op[2]);
  or or_1 (MUXimm[0], and_1_out, and_2_out);

  // Notes on the sheet:
  //   0 => OPERAND2
  //   1 => OPERAND0
  //   2 => PC+1
  //   Dans cet ordre pour minimiser le nombre de portes logiques
endmodule

module CTL3 (
  input  [2:0] op,
  input  EQ,
  output [1:0] MUXpc,
  output [1:0] FUNCalu
);

  wire and_4_out, and_5_out;

  and and_1 (MUXpc[0], op[2], op[1], op[0]);
  and and_2 (MUXpc[1], op[2], op[1], ~op[0], EQ);  // AND_Gate
  and and_3 (FUNCalu[0], op[1], ~op[0]);  // AND_Gate
  and and_4 (and_4_out, op[2], op[1]);
  and and_5 (and_5_out, op[1], op[0]);
  or or_1 (FUNCalu[1], and_4_out, and_5_out);

  // Notes on the sheet:
  //   0 => PC+1
  //   1 => OPERAND1
  //   2 => PC+1+OPERAND2
  //   Add, addi, sw, lw => 0 (add)
  //   Nand => 1 (nand)
  //   lui, jalr => 2 (transmission de OPERAND2)
  //   beq => 3 (calcul de EQ!)
endmodule

module reg16 (
  input  [15:0] IN,
  input  CLK,
  output [15:0] OUT
);

  Register #(.width(16)) register_1 (.D(IN), .en(1'b1), .Q(OUT), .clk(CLK));  // open: clr
endmodule

module ALU (
  input  [15:0] SCR1,
  input  [15:0] SCR2,
  input  [1:0] FUNCalu,
  output EQ,
  output [15:0] out
);

  wire [15:0] adder_1_out, nand_1_out, xnor_1_out;

  Adder #(.width(16)) adder_1 (.a(SCR1), .b(SCR2), .out(adder_1_out));  // open: cin, cout
  assign nand_1_out = ~(SCR2 & SCR1);  // NAND_Gate nand_1, 16 bits wide
  Multiplexer #(.select(2), .width(16)) multiplexer_1 (
    .in0(adder_1_out), .in1(nand_1_out), .in2(SCR2), .in3(SCR2), .out(out), .sel(FUNCalu));  // open: en
  assign xnor_1_out = ~(SCR1 ^ SCR2);  // XNOR_Gate xnor_1, 16 bits wide
  and and_1 (EQ, xnor_1_out[0], xnor_1_out[1], xnor_1_out[2], xnor_1_out[3], xnor_1_out[4], xnor_1_out[5], xnor_1_out[6], xnor_1_out[7], xnor_1_out[8], xnor_1_out[9], xnor_1_out[10], xnor_1_out[11], xnor_1_out[12], xnor_1_out[13], xnor_1_out[14], xnor_1_out[15]);
endmodule

module EXE (
  input  rT,
  input  [2:0] op,
  input  [15:0] OPERAND2,
  input  [15:0] OPERAND0,
  input  [15:0] OPERAND1,
  input  [15:0] PC,
  output rT_2,
  output [2:0] op_2,
  output [1:0] MUXpc,
  output [15:0] STORE_DATA,
  output [15:0] ALU_OUTPUT,
  output [15:0] OPERAND1_2,
  output [15:0] PC_1_Imm,
  output [15:0] PC_2
);

  wire alu_1_eq;
  wire [1:0] ctl3_1_funcalu, ctl4_1_muximm;
  wire [15:0] adder_1_out, multiplexer_1_out;

  Adder #(.width(16)) adder_1 (.a(PC), .b(16'h1), .out(adder_1_out));  // open: cin, cout
  CTL4 ctl4_1 (.op(op), .MUXimm(ctl4_1_muximm));
  Multiplexer #(.select(2), .width(16)) multiplexer_1 (
    .in0(OPERAND2), .in1(OPERAND0), .in2(adder_1_out), .out(multiplexer_1_out), .sel(ctl4_1_muximm));  // open: in3, en
  Adder #(.width(16)) adder_2 (.a(OPERAND0), .b(adder_1_out), .out(PC_1_Imm));  // open: cin, cout
  CTL3 ctl3_1 (.op(op), .EQ(alu_1_eq), .MUXpc(MUXpc), .FUNCalu(ctl3_1_funcalu));
  ALU alu_1 (.SCR1(multiplexer_1_out), .SCR2(OPERAND1), .FUNCalu(ctl3_1_funcalu), .out(ALU_OUTPUT), .EQ(alu_1_eq));

  assign op_2 = op;
  assign OPERAND1_2 = OPERAND1;
  assign PC_2 = PC;
  assign rT_2 = rT;
  assign STORE_DATA = OPERAND2;
endmodule

module WB (
  input  [2:0] rT_in,
  input  [15:0] RF_WRITE_DATA_in,
  output [2:0] rT_out,
  output WErt,
  output [15:0] TGT,
  output [15:0] RF_WRITE_DATA_out
);

  or or_1 (WErt, rT_in[0], rT_in[1], rT_in[2]);

  assign RF_WRITE_DATA_out = RF_WRITE_DATA_in;
  assign rT_out = rT_in;
  assign TGT = RF_WRITE_DATA_in;
endmodule
