// Logisim project ProcoDeal.circ as structural Verilog: 24 circuits, main circuit main
module main (
);

  wire AJ, clock_1_out, demultiplexer_1_out0, demultiplexer_1_out1, demultiplexer_1_out2,
       demultiplexer_1_out3, keyboard_1_avail, memkeyboard_1_clear, memkeyboard_1_clock,
       memkeyboard_1_rdenable, memtty_1_clear, memtty_1_clock, memtty_1_wtenable, WB_wert, WE;
  wire [1:0] AK, AT, exe_1_muxpc;
  wire [2:0] exe_1_op_2, exe_1_rt_2, ID_op, ID_rt, ID_s1, ID_s2, MEM_rt_2, memselect_1_out_2, reg3_1_out,
       reg3_2_out, reg3_3_out, reg3_4_out, reg3_5_out, reg3_6_out, reg3_7_out, reg3_8_out, WB_rt_out;
  wire [3:0] joystick_1_x, joystick_1_y, memselect_1_adrled;
  wire [6:0] keyboard_1_data, memtty_1_char;
  wire [15:0] data_memory_1_data_out, DIN, exe_1_alu_output, exe_1_operand1_2, exe_1_pc_1_imm, exe_1_pc_2,
       exe_1_store_data, ID_ope0, ID_pc_out, ID_src1, ID_src2, IF_ins, IF_pc_1, IF_pc_2, MEM_rf_write_data,
       memjoy_1_out_4, memkeyboard_1_memout, memled_1_data_out, memled_1_out_5, memled_1_out_6,
       memled_1_out_7, memled_1_out_8, memled_1_out_9, memled_1_out_10, memled_1_out_11, memled_1_out_12,
       memled_1_out_14, memled_1_out_15, memled_1_out_16, memled_1_out_17, memled_1_out_18, memled_1_out_19,
       memled_1_out_20, memled_1_out_21, memselect_1_adrram, memtty_1_memout, multiplexer_1_out,
       multiplexer_2_out, reg16_1_out, reg16_2_out, reg16_3_out, reg16_4_out, reg16_5_out, reg16_6_out,
       reg16_7_out, reg16_8_out, reg16_10_out, reg16_11_out, reg16_12_out, WB_rf_write_data_out, WB_tgt;

  Clock clock_1 (.out(clock_1_out));
  reg3 reg3_1 (.IN(ID_rt), .OUT(reg3_1_out), .CLK(clock_1_out));
  reg3 reg3_2 (.IN(ID_op), .OUT(reg3_2_out), .CLK(clock_1_out));
  Multiplexer #(.select(2), .width(16), .enable("false")) multiplexer_1 (
    .in0(IF_pc_1), .in1(exe_1_operand1_2), .in2(exe_1_pc_1_imm), .in3({16{1'b0}}), .out(multiplexer_1_out),
    .sel(exe_1_muxpc));
  reg16 reg16_1 (.IN(multiplexer_1_out), .OUT(reg16_1_out), .CLK(clock_1_out));
  IF IF (.PC(reg16_1_out), .INS(IF_ins), .PC_2(IF_pc_2), .PC_1(IF_pc_1));
  reg16 reg16_2 (.IN(IF_ins), .OUT(reg16_2_out), .CLK(clock_1_out));
  reg16 reg16_3 (.IN(IF_pc_2), .OUT(reg16_3_out), .CLK(clock_1_out));
  ID ID (
    .PC_in(reg16_3_out), .INS(reg16_2_out), .TGT_sel(WB_rt_out), .WE(WB_wert), .PC_out(ID_pc_out),
    .OP(ID_op), .rT(ID_rt), .TGT(WB_tgt), .SRC1(ID_src1), .SRC2(ID_src2), .ope0(ID_ope0), .s1(ID_s1),
    .s2(ID_s2));
  reg3 reg3_3 (.IN(ID_s2), .OUT(reg3_3_out), .CLK(clock_1_out));
  reg3 reg3_4 (.IN(ID_s1), .OUT(reg3_4_out), .CLK(clock_1_out));
  reg16 reg16_4 (.IN(ID_pc_out), .OUT(reg16_4_out), .CLK(clock_1_out));
  reg16 reg16_5 (.IN(ID_ope0), .OUT(reg16_5_out), .CLK(clock_1_out));
  EXE exe_1 (
    .rT(reg3_1_out), .op(reg3_2_out), .OPERAND2(reg16_8_out), .OPERAND0(reg16_5_out), .OPERAND1(reg16_7_out),
    .PC(reg16_4_out), .rT_2(exe_1_rt_2), .op_2(exe_1_op_2), .MUXpc(exe_1_muxpc),
    .STORE_DATA(exe_1_store_data), .ALU_OUTPUT(exe_1_alu_output), .OPERAND1_2(exe_1_operand1_2),
    .PC_1_Imm(exe_1_pc_1_imm), .PC_2(exe_1_pc_2), .EXE_bypass(reg16_10_out), .MEM_bypass(reg16_11_out),
    .WB_bypass(reg16_12_out), .EXE_rT(reg3_5_out), .MEM_rT(reg3_7_out), .WB_rT(reg3_8_out), .s1(reg3_4_out),
    .s2(reg3_3_out));
  reg3 reg3_5 (.IN(exe_1_rt_2), .OUT(reg3_5_out), .CLK(clock_1_out));
  reg3 reg3_6 (.IN(exe_1_op_2), .OUT(reg3_6_out), .CLK(clock_1_out));
  reg16 reg16_6 (.IN(exe_1_pc_2), .OUT(reg16_6_out), .CLK(clock_1_out));
  MEM MEM (
    .op(reg3_6_out), .WE(WE), .rT(reg3_5_out), .rT_2(MEM_rt_2), .PC(reg16_6_out),
    .READ_DATA(multiplexer_2_out), .RF_WRITE_DATA(MEM_rf_write_data), .ALU_OUTPUT(reg16_10_out));
  reg3 reg3_7 (.IN(MEM_rt_2), .OUT(reg3_7_out), .CLK(clock_1_out));
  reg3 reg3_8 (.IN(WB_rt_out), .OUT(reg3_8_out), .CLK(clock_1_out));
  reg16 reg16_7 (.IN(ID_src1), .OUT(reg16_7_out), .CLK(clock_1_out));
  reg16 reg16_8 (.IN(ID_src2), .OUT(reg16_8_out), .CLK(clock_1_out));
  reg16 reg16_9 (.IN(exe_1_store_data), .OUT(DIN), .CLK(clock_1_out));
  reg16 reg16_10 (.IN(exe_1_alu_output), .OUT(reg16_10_out), .CLK(clock_1_out));
  reg16 reg16_11 (.IN(MEM_rf_write_data), .OUT(reg16_11_out), .CLK(clock_1_out));
  WB WB (
    .rT_in(reg3_7_out), .RF_WRITE_DATA_in(reg16_11_out), .rT_out(WB_rt_out), .WErt(WB_wert), .TGT(WB_tgt),
    .RF_WRITE_DATA_out(WB_rf_write_data_out));
  reg16 reg16_12 (.IN(WB_rf_write_data_out), .OUT(reg16_12_out), .CLK(clock_1_out));
  MEMSELECT memselect_1 (
    .ADR(reg16_10_out), .out_2(memselect_1_out_2), .ADRRAM(memselect_1_adrram), .ADRLED(memselect_1_adrled),
    .ADRKEY(AK), .ADRTTY(AT), .ADRJOY(AJ));
  Multiplexer #(.select(3), .width(16), .enable("false")) multiplexer_2 (
    .in0(data_memory_1_data_out), .in1(memled_1_data_out), .in2(memkeyboard_1_memout), .in3(memtty_1_memout),
    .in4(memjoy_1_out_4), .out(multiplexer_2_out), .sel(memselect_1_out_2));  // open: in5, in6, in7
  DATA_MEMORY data_memory_1 (
    .DATA_IN(DIN), .ADDR(memselect_1_adrram), .WE(WE), .DATA_OUT(data_memory_1_data_out),
    .EN(demultiplexer_1_out0));
  MEMJOY memjoy_1 (.ABS_JOY(joystick_1_x), .ORD_JOY(joystick_1_y), .ADR(AJ), .out_4(memjoy_1_out_4));
  Joystick joystick_1 (.x(joystick_1_x), .y(joystick_1_y));
  Demultiplexer #(.select(3), .enable("false")) demultiplexer_1 (
    .out0(demultiplexer_1_out0), .out1(demultiplexer_1_out1), .out2(demultiplexer_1_out2),
    .out3(demultiplexer_1_out3), .in(1'b1), .sel(memselect_1_out_2));  // open: out4, out5, out6, out7
  DotMatrix #(.matrixcols(16), .matrixrows(16)) dotmatrix_1 (
    .col0(memled_1_out_5), .col1(memled_1_out_6), .col2(memled_1_out_7), .col3(memled_1_out_8),
    .col4(memled_1_out_9), .col5(memled_1_out_10), .col6(memled_1_out_11), .col7(memled_1_out_12),
    .col8(memled_1_out_14), .col9(memled_1_out_15), .col10(memled_1_out_16), .col11(memled_1_out_17),
    .col12(memled_1_out_18), .col13(memled_1_out_19), .col14(memled_1_out_20), .col15(memled_1_out_21));
  MEMLED memled_1 (
    .WE(WE), .DATA_IN(DIN), .ADR(memselect_1_adrled), .out_5(memled_1_out_5), .out_6(memled_1_out_6),
    .out_7(memled_1_out_7), .out_8(memled_1_out_8), .out_9(memled_1_out_9), .out_10(memled_1_out_10),
    .out_11(memled_1_out_11), .out_12(memled_1_out_12), .DATA_OUT(memled_1_data_out),
    .out_14(memled_1_out_14), .out_15(memled_1_out_15), .out_16(memled_1_out_16), .out_17(memled_1_out_17),
    .out_18(memled_1_out_18), .out_19(memled_1_out_19), .out_20(memled_1_out_20), .out_21(memled_1_out_21),
    .EN(demultiplexer_1_out1));
  MEMTTY memtty_1 (
    .VALIN(DIN), .ADR(AT), .CLOCK(memtty_1_clock), .WTENABLE(memtty_1_wtenable), .CLEAR(memtty_1_clear),
    .CHAR(memtty_1_char), .MEMOUT(memtty_1_memout), .EN(demultiplexer_1_out3), .WE(WE));
  TTY tty_1 (.data(memtty_1_char), .clk(memtty_1_clock), .we(memtty_1_wtenable), .clr(memtty_1_clear));
  Keyboard keyboard_1 (
    .clk(memkeyboard_1_clock), .re(memkeyboard_1_rdenable), .clr(memkeyboard_1_clear),
    .avail(keyboard_1_avail), .data(keyboard_1_data));
  MEMKEYBOARD memkeyboard_1 (
    .VALIN(DIN), .AV(keyboard_1_avail), .ADR(AK), .CHAR(keyboard_1_data), .CLOCK(memkeyboard_1_clock),
    .RDENABLE(memkeyboard_1_rdenable), .CLEAR(memkeyboard_1_clear), .WE(WE), .MEMOUT(memkeyboard_1_memout),
    .EN(demultiplexer_1_out2));

  // Notes on the sheet:
  //   EXE
endmodule

module IF (
  input  [15:0] PC,
  output [15:0] INS,
  output [15:0] PC_2,
  output [15:0] PC_1
);

  ROM #(.addrWidth(16), .dataWidth(16)) rom_1 (.addr(PC), .data(INS), .sel(1'b1));
  Adder #(.width(16)) adder_1 (.a(PC), .b(16'h1), .out(PC_1));  // open: cin, cout

  assign PC_2 = PC;

  // Notes on the sheet:
  //   contents of rom_1 (hex, n*v repeats v):
  //   73ff 3236 3401 b600 9602 0 0 0 d47b 0 0 9603 73ff 323a 7800 3b01 ba00 b602 73ff 323e 9600 73ff 3226
  //   1205 77ff 36bf b600 241c e080
endmodule

module ID (
  input  [15:0] PC_in,
  input  [15:0] INS,
  input  [2:0] TGT_sel,
  input  [15:0] TGT,
  input  WE,
  output [15:0] PC_out,
  output [2:0] OP,
  output [2:0] rT,
  output [15:0] SRC1,
  output [15:0] SRC2,
  output [15:0] ope0,
  output [2:0] s1,
  output [2:0] s2
);

  wire ctl6_1_op0, ctl6_1_s2;
  wire [15:0] left_shift_6_1_out, sign_ext_7_1_out;

  Sign_Ext_7 sign_ext_7_1 (.in(INS[9:0]), .out(sign_ext_7_1_out));
  Left_shift_6 left_shift_6_1 (.in(INS[9:0]), .out(left_shift_6_1_out));
  CTL7 ctl7_1 (.OP_in(INS[15:13]), .rA(INS[12:10]), .OP_out(OP), .rT(rT));
  CTL6 ctl6_1 (.OP(OP), .s2(ctl6_1_s2), .op0(ctl6_1_op0));
  Multiplexer #(.width(3), .enable("false")) multiplexer_1 (
    .in0(INS[12:10]), .in1(INS[2:0]), .out(s2), .sel(ctl6_1_s2));
  Multiplexer #(.width(16), .enable("false")) multiplexer_2 (
    .in0(sign_ext_7_1_out), .in1(left_shift_6_1_out), .out(ope0), .sel(ctl6_1_op0));
  RegisterFile registerfile_1 (
    .SRC1_in(INS[9:7]), .WE(WE), .SRC2_in(s2), .TGT_sel(TGT_sel), .TGT_in(TGT), .SRC1_out(SRC1),
    .SRC2_out(SRC2));

  assign PC_out = PC_in;
  assign s1 = INS[9:7];
endmodule

module RegisterFile (
  input  [2:0] TGT_sel,
  input  [15:0] TGT_in,
  input  [2:0] SRC1_in,
  input  WE,
  input  [2:0] SRC2_in,
  output [15:0] SRC1_out,
  output [15:0] SRC2_out
);

  wire demultiplexer_1_out1, demultiplexer_1_out2, demultiplexer_1_out3, demultiplexer_1_out4,
       demultiplexer_1_out5, demultiplexer_1_out6, demultiplexer_1_out7;
  wire [15:0] demultiplexer_2_out1, demultiplexer_2_out2, demultiplexer_2_out3, demultiplexer_2_out4,
       demultiplexer_2_out5, demultiplexer_2_out6, demultiplexer_2_out7, register_1_q, register_2_q,
       register_3_q, register_4_q, register_5_q, register_6_q, register_7_q, register_8_q;

  Demultiplexer #(.select(3)) demultiplexer_1 (
    .out1(demultiplexer_1_out1), .out2(demultiplexer_1_out2), .out3(demultiplexer_1_out3),
    .out4(demultiplexer_1_out4), .out5(demultiplexer_1_out5), .out6(demultiplexer_1_out6),
    .out7(demultiplexer_1_out7), .in(WE), .sel(TGT_sel));  // open: out0, en
  Register #(.width(16), .trigger("high")) register_1 (.D({16{1'b0}}), .Q(register_1_q));  // open: en, clk, clr
  Demultiplexer #(.select(3), .width(16)) demultiplexer_2 (
    .out1(demultiplexer_2_out1), .out2(demultiplexer_2_out2), .out3(demultiplexer_2_out3),
    .out4(demultiplexer_2_out4), .out5(demultiplexer_2_out5), .out6(demultiplexer_2_out6),
    .out7(demultiplexer_2_out7), .in(TGT_in), .sel(TGT_sel));  // open: out0, en
  Register #(.width(16), .trigger("high")) register_2 (
    .D(demultiplexer_2_out1), .Q(register_2_q), .clk(demultiplexer_1_out1));  // open: en, clr
  Register #(.width(16), .trigger("high")) register_3 (
    .D(demultiplexer_2_out2), .Q(register_3_q), .clk(demultiplexer_1_out2));  // open: en, clr
  Register #(.width(16), .trigger("high")) register_4 (
    .D(demultiplexer_2_out3), .Q(register_4_q), .clk(demultiplexer_1_out3));  // open: en, clr
  Register #(.width(16), .trigger("high")) register_5 (
    .D(demultiplexer_2_out4), .Q(register_5_q), .clk(demultiplexer_1_out4));  // open: en, clr
  Register #(.width(16), .trigger("high")) register_6 (
    .D(demultiplexer_2_out5), .Q(register_6_q), .clk(demultiplexer_1_out5));  // open: en, clr
  Register #(.width(16), .trigger("high")) register_7 (
    .D(demultiplexer_2_out7), .Q(register_7_q), .clk(demultiplexer_1_out7));  // open: en, clr
  Register #(.width(16), .trigger("high")) register_8 (
    .D(demultiplexer_2_out6), .Q(register_8_q), .clk(demultiplexer_1_out6));  // open: en, clr
  Multiplexer #(.select(3), .width(16)) multiplexer_1 (
    .in0(register_1_q), .in1(register_2_q), .in2(register_3_q), .in3(register_4_q), .in4(register_5_q),
    .in5(register_6_q), .in6(register_8_q), .in7(register_7_q), .out(SRC1_out), .sel(SRC1_in));  // open: en
  Multiplexer #(.select(3), .width(16)) multiplexer_2 (
    .in0(register_1_q), .in1(register_2_q), .in2(register_3_q), .in3(register_4_q), .in4(register_5_q),
    .in5(register_6_q), .in6(register_8_q), .in7(register_7_q), .out(SRC2_out), .sel(SRC2_in));  // open: en
endmodule

module CTL7 (
  input  [2:0] OP_in,
  input  [2:0] rA,
  output [2:0] OP_out,
  output [2:0] rT
);

  wire and_1_out, and_2_out, and_3_out, not_1_out;

  and and_1 (and_1_out, OP_in[2], ~OP_in[1], OP_in[0]);  // AND_Gate
  and and_2 (and_2_out, ~and_1_out, ~and_3_out);  // AND_Gate
  assign rT = and_2_out ? rA : 3'bz;  // Controlled_Buffer controlled_buffer_1
  and and_3 (and_3_out, ~OP_in[0], OP_in[1], OP_in[2]);  // AND_Gate
  not not_1 (not_1_out, and_2_out);
  assign rT = not_1_out ? 3'b000 : 3'bz;  // Controlled_Buffer controlled_buffer_2

  assign OP_out = OP_in;
endmodule

module CTL6 (
  input  [2:0] OP,
  output s2,
  output op0
);

  and and_1 (s2, ~OP[0], ~OP[2]);  // AND_Gate
  and and_2 (op0, OP[0], OP[1], ~OP[2]);  // AND_Gate

  // Notes on the sheet:
  //   0 => rA
  //   1 => RC
  //   1 => Left-Shift 6
endmodule

module Left_shift_6 (
  input  [9:0] in,
  output [15:0] out
);


  assign out = {in, {6{1'b0}}};
endmodule

module Sign_Ext_7 (
  input  [9:0] in,
  output [15:0] out
);


  assign out = {{10{in[6]}}, in[5:0]};
endmodule

module CTL4 (
  input  [2:0] op,
  output [1:0] MUXimm
);

  wire and_1_out, and_2_out;

  and and_1 (and_1_out, op[2], ~op[1]);  // AND_Gate
  and and_2 (and_2_out, ~op[2], op[0]);  // AND_Gate
  and and_3 (MUXimm[1], op[0], op[1], op[2]);
  or or_1 (MUXimm[0], and_1_out, and_2_out);

  // Notes on the sheet:
  //   0 => OPERAND2
  //   1 => OPERAND0
  //   2 => PC+1
  //   Dans cet ordre pour minimiser le nombre de portes logiques
endmodule

module CTL3 (
  input  [2:0] op,
  input  EQ,
  output [1:0] MUXpc,
  output [1:0] FUNCalu
);

  wire and_4_out, and_5_out;

  and and_1 (MUXpc[0], op[2], op[1], op[0]);
  and and_2 (MUXpc[1], op[2], op[1], ~op[0], EQ);  // AND_Gate
  and and_3 (FUNCalu[0], op[1], ~op[0]);  // AND_Gate
  and and_4 (and_4_out, op[2], op[1]);
  and and_5 (and_5_out, op[1], op[0]);
  or or_1 (FUNCalu[1], and_4_out, and_5_out);

  // Notes on the sheet:
  //   0 => PC+1
  //   1 => OPERAND1
  //   2 => PC+1+OPERAND2
  //   Add, addi, sw, lw => 0 (add)
  //   Nand => 1 (nand)
  //   lui, jalr => 2 (transmission de OPERAND2)
  //   beq => 3 (calcul de EQ!)
endmodule

module reg16 (
  input  [15:0] IN,
  input  CLK,
  output [15:0] OUT
);

  Register #(.width(16)) register_1 (.D(IN), .en(1'b1), .Q(OUT), .clk(CLK));  // open: clr
endmodule

module ALU (
  input  [15:0] SCR1,
  input  [15:0] SCR2,
  input  [1:0] FUNCalu,
  output EQ,
  output [15:0] out
);

  wire [15:0] adder_1_out, nand_1_out, xnor_1_out;

  Adder #(.width(16)) adder_1 (.a(SCR1), .b(SCR2), .out(adder_1_out));  // open: cin, cout
  and and_1 (EQ, xnor_1_out[0], xnor_1_out[1], xnor_1_out[2], xnor_1_out[3], xnor_1_out[4], xnor_1_out[5], xnor_1_out[6], xnor_1_out[7], xnor_1_out[8], xnor_1_out[9], xnor_1_out[10], xnor_1_out[11], xnor_1_out[12], xnor_1_out[13], xnor_1_out[14], xnor_1_out[15]);
  assign nand_1_out = ~(SCR2 & SCR1);  // NAND_Gate nand_1, 16 bits wide
  Multiplexer #(.select(2), .width(16)) multiplexer_1 (
    .in0(adder_1_out), .in1(nand_1_out), .in2(SCR2), .in3(SCR2), .out(out), .sel(FUNCalu));  // open: en
  assign xnor_1_out = ~(SCR1 ^ SCR2);  // XNOR_Gate xnor_1, 16 bits wide
endmodule

module EXE (
  input  [15:0] EXE_bypass,
  input  [15:0] MEM_bypass,
  input  [15:0] WB_bypass,
  input  [2:0] EXE_rT,
  input  [2:0] MEM_rT,
  input  [2:0] WB_rT,
  input  [2:0] s1,
  input  [2:0] s2,
  input  [2:0] rT,
  input  [2:0] op,
  input  [15:0] OPERAND2,
  input  [15:0] OPERAND0,
  input  [15:0] OPERAND1,
  input  [15:0] PC,
  output [2:0] rT_2,
  output [2:0] op_2,
  output [1:0] MUXpc,
  output [15:0] STORE_DATA,
  output [15:0] ALU_OUTPUT,
  output [15:0] OPERAND1_2,
  output [15:0] PC_1_Imm,
  output [15:0] PC_2
);

  wire alu_1_eq;
  wire [1:0] ctl3_1_funcalu, ctl4_1_muximm, ctl5_1_mux_alu1, ctl5_1_mux_alu2;
  wire [15:0] adder_1_out, multiplexer_3_out;

  CTL5 ctl5_1 (
    .s1(s1), .EXE_rT(EXE_rT), .MEM_rT(MEM_rT), .WB_rT(WB_rT), .s2(s2), .MUX_alu1(ctl5_1_mux_alu1),
    .MUX_alu2(ctl5_1_mux_alu2));
  CTL4 ctl4_1 (.op(op), .MUXimm(ctl4_1_muximm));
  Multiplexer #(.select(2), .width(16)) multiplexer_1 (
    .in0(OPERAND2), .in1(EXE_bypass), .in2(MEM_bypass), .in3(WB_bypass), .out(STORE_DATA),
    .sel(ctl5_1_mux_alu2));  // open: en
  Multiplexer #(.select(2), .width(16)) multiplexer_2 (
    .in0(OPERAND1), .in1(EXE_bypass), .in2(MEM_bypass), .in3(WB_bypass), .out(OPERAND1_2),
    .sel(ctl5_1_mux_alu1));  // open: en
  Adder #(.width(16)) adder_1 (.a(PC), .b(16'h1), .out(adder_1_out));  // open: cin, cout
  Multiplexer #(.select(2), .width(16)) multiplexer_3 (
    .in0(STORE_DATA), .in1(OPERAND0), .in2(adder_1_out), .out(multiplexer_3_out), .sel(ctl4_1_muximm));  // open: in3, en
  Adder #(.width(16)) adder_2 (.a(OPERAND0), .b(adder_1_out), .out(PC_1_Imm));  // open: cin, cout
  CTL3 ctl3_1 (.op(op), .EQ(alu_1_eq), .MUXpc(MUXpc), .FUNCalu(ctl3_1_funcalu));
  ALU alu_1 (.SCR1(OPERAND1_2), .SCR2(multiplexer_3_out), .FUNCalu(ctl3_1_funcalu), .EQ(alu_1_eq), .out(ALU_OUTPUT));

  assign op_2 = op;
  assign PC_2 = PC;
  assign rT_2 = rT;
endmodule

module DATA_MEMORY (
  input  [15:0] DATA_IN,
  input  [15:0] ADDR,
  input  EN,
  input  WE,
  output [15:0] DATA_OUT
);

  wire clock_1_out, not_1_out;
  wire [15:0] register_1_q;

  Clock clock_1 (.out(clock_1_out));
  Register #(.width(16), .trigger("falling")) register_1 (
    .D(DATA_IN), .en(1'b1), .Q(register_1_q), .clk(clock_1_out));  // open: clr
  assign DATA_OUT = WE ? register_1_q : 16'bz;  // Controlled_Buffer controlled_buffer_1
  not not_1 (not_1_out, WE);
  RAM #(.addrWidth(16), .dataWidth(16), .bus("asynch")) ram_1 (
    .addr(ADDR), .data(DATA_OUT), .sel(EN), .ld(not_1_out));  // open: clr
endmodule

module WB (
  input  [2:0] rT_in,
  input  [15:0] RF_WRITE_DATA_in,
  output [2:0] rT_out,
  output WErt,
  output [15:0] TGT,
  output [15:0] RF_WRITE_DATA_out
);

  or or_1 (WErt, rT_in[0], rT_in[1], rT_in[2]);

  assign RF_WRITE_DATA_out = RF_WRITE_DATA_in;
  assign rT_out = rT_in;
  assign TGT = RF_WRITE_DATA_in;
endmodule

module reg3 (
  input  [2:0] IN,
  input  CLK,
  output [2:0] OUT
);

  Register #(.width(3)) register_1 (.D(IN), .en(1'b1), .Q(OUT), .clk(CLK));  // open: clr
endmodule

module CTL2 (
  input  [2:0] op,
  output WEdmem,
  output MUXout
);

  wire comparator_2_eq;

  Comparator #(.width(3), .mode("unsigned")) comparator_1 (.a(op), .b(3'b101), .eq(WEdmem));  // open: gt, lt
  not not_1 (MUXout, comparator_2_eq);
  Comparator #(.width(3), .mode("unsigned")) comparator_2 (.a(op), .b(3'b100), .eq(comparator_2_eq));  // open: gt, lt
endmodule

module MEM (
  input  [2:0] op,
  input  [2:0] rT,
  input  [15:0] PC,
  input  [15:0] READ_DATA,
  input  [15:0] ALU_OUTPUT,
  output WE,
  output [2:0] rT_2,
  output [15:0] RF_WRITE_DATA
);

  wire ctl2_1_muxout;

  CTL2 ctl2_1 (.op(op), .WEdmem(WE), .MUXout(ctl2_1_muxout));
  Multiplexer #(.width(16)) multiplexer_1 (
    .in0(READ_DATA), .in1(ALU_OUTPUT), .out(RF_WRITE_DATA), .sel(ctl2_1_muxout));  // open: en

  assign rT_2 = rT;

  // Notes on the sheet:
  //   La manche
endmodule

module CTL5 (
  input  [2:0] s1,
  input  [2:0] EXE_rT,
  input  [2:0] MEM_rT,
  input  [2:0] WB_rT,
  input  [2:0] s2,
  output [1:0] MUX_alu1,
  output [1:0] MUX_alu2
);

  wire and_1_out, and_2_out, and_3_out, and_4_out, and_5_out, and_6_out, and_7_out, and_8_out,
       comparator_1_eq, comparator_2_eq, comparator_3_eq, comparator_4_eq, comparator_5_eq, comparator_6_eq,
       comparator_7_eq, comparator_8_eq;

  Comparator #(.width(3)) comparator_1 (.a(s1), .b(3'b000), .eq(comparator_1_eq));  // open: gt, lt
  Comparator #(.width(3)) comparator_2 (.a(s1), .b(EXE_rT), .eq(comparator_2_eq));  // open: gt, lt
  Comparator #(.width(3)) comparator_3 (.a(s1), .b(MEM_rT), .eq(comparator_3_eq));  // open: gt, lt
  Comparator #(.width(3)) comparator_4 (.a(s1), .b(WB_rT), .eq(comparator_4_eq));  // open: gt, lt
  Comparator #(.width(3)) comparator_5 (.a(WB_rT), .b(s2), .eq(comparator_5_eq));  // open: gt, lt
  Comparator #(.width(3)) comparator_6 (.a(MEM_rT), .b(s2), .eq(comparator_6_eq));  // open: gt, lt
  Comparator #(.width(3)) comparator_7 (.a(EXE_rT), .b(s2), .eq(comparator_7_eq));  // open: gt, lt
  Comparator #(.width(3)) comparator_8 (.a(3'b000), .b(s2), .eq(comparator_8_eq));  // open: gt, lt
  and and_1 (and_1_out, ~comparator_1_eq, comparator_2_eq);  // AND_Gate
  or or_1 (MUX_alu1[0], and_1_out, and_2_out);
  and and_2 (and_2_out, ~comparator_1_eq, ~comparator_3_eq, comparator_4_eq);  // AND_Gate
  and and_3 (and_3_out, ~comparator_1_eq, ~comparator_2_eq, comparator_3_eq);  // AND_Gate
  or or_2 (MUX_alu1[1], and_3_out, and_4_out);
  and and_4 (and_4_out, ~comparator_1_eq, ~comparator_2_eq, comparator_4_eq);  // AND_Gate
  and and_5 (and_5_out, comparator_5_eq, ~comparator_7_eq, ~comparator_8_eq);  // AND_Gate
  or or_3 (MUX_alu2[1], and_5_out, and_6_out);
  and and_6 (and_6_out, comparator_6_eq, ~comparator_7_eq, ~comparator_8_eq);  // AND_Gate
  and and_7 (and_7_out, comparator_5_eq, ~comparator_6_eq, ~comparator_8_eq);  // AND_Gate
  or or_4 (MUX_alu2[0], and_7_out, and_8_out);
  and and_8 (and_8_out, comparator_7_eq, ~comparator_8_eq);  // AND_Gate
endmodule

module MEMSELECT (
  input  [15:0] ADR,
  output [2:0] out_2,
  output [15:0] ADRRAM,
  output [3:0] ADRLED,
  output [1:0] ADRKEY,
  output [1:0] ADRTTY,
  output ADRJOY
);

  wire and_1_out, and_2_out, and_3_out, comparator_1_lt, comparator_2_lt, comparator_3_lt, comparator_4_lt,
       not_1_out, subtractor_1_bout, subtractor_2_bout, subtractor_3_bout;
  wire [15:1] subtractor_4_out;
  wire [15:2] subtractor_2_out, subtractor_3_out;
  wire [15:4] subtractor_1_out;

  Subtractor #(.width(16)) subtractor_1 (
    .a(ADR), .b(16'hffe6), .out({subtractor_1_out, ADRLED}), .bout(subtractor_1_bout));  // open: bin
  Subtractor #(.width(16)) subtractor_2 (
    .a(ADR), .b(16'hfff6), .out({subtractor_2_out, ADRKEY}), .bin(subtractor_1_bout), .bout(subtractor_2_bout));
  Subtractor #(.width(16)) subtractor_3 (
    .a(ADR), .b(16'hfffa), .out({subtractor_3_out, ADRTTY}), .bin(subtractor_2_bout), .bout(subtractor_3_bout));
  Subtractor #(.width(16)) subtractor_4 (
    .a(ADR), .b(16'hfffe), .out({subtractor_4_out, ADRJOY}), .bin(subtractor_3_bout));  // open: bout
  Comparator #(.width(16), .mode("unsigned")) comparator_1 (
    .a(ADR), .b(16'hffe6), .lt(comparator_1_lt));  // open: gt, eq
  assign out_2 = comparator_1_lt ? 3'b000 : 3'bz;  // Controlled_Buffer controlled_buffer_1
  Comparator #(.width(16), .mode("unsigned")) comparator_2 (
    .a(ADR), .b(16'hfff6), .lt(comparator_2_lt));  // open: gt, eq
  and and_1 (and_1_out, ~comparator_1_lt, comparator_2_lt);  // AND_Gate
  assign out_2 = and_1_out ? 3'b001 : 3'bz;  // Controlled_Buffer controlled_buffer_2
  Comparator #(.width(16), .mode("unsigned")) comparator_3 (
    .a(ADR), .b(16'hfffa), .lt(comparator_3_lt));  // open: gt, eq
  and and_2 (and_2_out, ~comparator_2_lt, comparator_3_lt);  // AND_Gate
  assign out_2 = and_2_out ? 3'b010 : 3'bz;  // Controlled_Buffer controlled_buffer_3
  Comparator #(.width(16), .mode("unsigned")) comparator_4 (
    .a(ADR), .b(16'hfffe), .lt(comparator_4_lt));  // open: gt, eq
  not not_1 (not_1_out, comparator_4_lt);
  and and_3 (and_3_out, ~comparator_3_lt, comparator_4_lt);  // AND_Gate
  assign out_2 = and_3_out ? 3'b011 : 3'bz;  // Controlled_Buffer controlled_buffer_4
  assign out_2 = not_1_out ? 3'b100 : 3'bz;  // Controlled_Buffer controlled_buffer_5

  assign ADRRAM = ADR;
endmodule

module MEMKEYBOARD (
  input  [15:0] VALIN,
  input  EN,
  input  AV,
  input  [1:0] ADR,
  input  WE,
  input  [6:0] CHAR,
  output CLOCK,
  output RDENABLE,
  output CLEAR,
  output [15:0] MEMOUT
);

  wire and_1_out, clock_1_out, clock_2_out, demultiplexer_1_out0, demultiplexer_1_out1, demultiplexer_1_out2,
       demultiplexer_1_out3;
  wire [15:0] register_4_q, register_5_q;
  wire [15:1] register_2_q, register_3_q;

  Demultiplexer #(.select(2), .enable("false")) demultiplexer_1 (
    .out0(demultiplexer_1_out0), .out1(demultiplexer_1_out1), .out2(demultiplexer_1_out2),
    .out3(demultiplexer_1_out3), .in(EN), .sel(ADR));
  Register #(.width(1), .trigger("falling")) register_1 (
    .D(demultiplexer_1_out3), .en(1'b1), .Q(CLOCK), .clk(clock_1_out));  // open: clr
  Clock clock_1 (.out(clock_1_out));
  Register #(.width(16)) register_2 (
    .D(VALIN), .en(demultiplexer_1_out0), .Q({register_2_q, RDENABLE}), .clk(and_1_out));  // open: clr
  Register #(.width(16)) register_3 (
    .D(VALIN), .en(demultiplexer_1_out1), .Q({register_3_q, CLEAR}), .clk(and_1_out));  // open: clr
  Register #(.width(16)) register_4 (
    .D({{15{1'b0}}, AV}), .en(demultiplexer_1_out2), .Q(register_4_q), .clk(demultiplexer_1_out2));  // open: clr
  Register #(.width(16)) register_5 (
    .D({{9{1'b0}}, CHAR}), .en(demultiplexer_1_out3), .Q(register_5_q), .clk(demultiplexer_1_out3));  // open: clr
  Multiplexer #(.select(2), .width(16), .enable("false")) multiplexer_1 (
    .in0({register_2_q, RDENABLE}), .in1({register_3_q, CLEAR}), .in2(register_4_q), .in3(register_5_q),
    .out(MEMOUT), .sel(ADR));
  and and_1 (and_1_out, ~clock_2_out, WE);  // AND_Gate
  Clock clock_2 (.out(clock_2_out));
endmodule

module MEMLED (
  input  WE,
  input  [15:0] DATA_IN,
  input  EN,
  input  [3:0] ADR,
  output [15:0] out_5,
  output [15:0] out_6,
  output [15:0] out_7,
  output [15:0] out_8,
  output [15:0] out_9,
  output [15:0] out_10,
  output [15:0] out_11,
  output [15:0] out_12,
  output [15:0] DATA_OUT,
  output [15:0] out_14,
  output [15:0] out_15,
  output [15:0] out_16,
  output [15:0] out_17,
  output [15:0] out_18,
  output [15:0] out_19,
  output [15:0] out_20,
  output [15:0] out_21
);

  wire clock_1_out, demultiplexer_1_out0, demultiplexer_1_out1, demultiplexer_1_out2, demultiplexer_1_out3,
       demultiplexer_1_out4, demultiplexer_1_out5, demultiplexer_1_out6, demultiplexer_1_out7,
       demultiplexer_1_out8, demultiplexer_1_out9, demultiplexer_1_out10, demultiplexer_1_out11,
       demultiplexer_1_out12, demultiplexer_1_out13, demultiplexer_1_out14, demultiplexer_1_out15,
       register_1_q;

  Demultiplexer #(.select(4), .enable("false")) demultiplexer_1 (
    .out0(demultiplexer_1_out0), .out1(demultiplexer_1_out1), .out2(demultiplexer_1_out2),
    .out3(demultiplexer_1_out3), .out4(demultiplexer_1_out4), .out5(demultiplexer_1_out5),
    .out6(demultiplexer_1_out6), .out7(demultiplexer_1_out7), .out8(demultiplexer_1_out8),
    .out9(demultiplexer_1_out9), .out10(demultiplexer_1_out10), .out11(demultiplexer_1_out11),
    .out12(demultiplexer_1_out12), .out13(demultiplexer_1_out13), .out14(demultiplexer_1_out14),
    .out15(demultiplexer_1_out15), .in(EN), .sel(ADR));
  Register #(.width(1), .trigger("falling")) register_1 (
    .D(WE), .Q(register_1_q), .clk(clock_1_out), .clr(clock_1_out));  // open: en
  Clock clock_1 (.out(clock_1_out));
  Register #(.width(16)) register_2 (
    .D(DATA_IN), .en(demultiplexer_1_out0), .Q(out_5), .clk(register_1_q));  // open: clr
  Register #(.width(16)) register_3 (
    .D(DATA_IN), .en(demultiplexer_1_out1), .Q(out_6), .clk(register_1_q));  // open: clr
  Register #(.width(16)) register_4 (
    .D(DATA_IN), .en(demultiplexer_1_out2), .Q(out_7), .clk(register_1_q));  // open: clr
  Register #(.width(16)) register_5 (
    .D(DATA_IN), .en(demultiplexer_1_out3), .Q(out_8), .clk(register_1_q));  // open: clr
  Register #(.width(16)) register_6 (
    .D(DATA_IN), .en(demultiplexer_1_out4), .Q(out_9), .clk(register_1_q));  // open: clr
  Register #(.width(16)) register_7 (
    .D(DATA_IN), .en(demultiplexer_1_out5), .Q(out_10), .clk(register_1_q));  // open: clr
  Register #(.width(16)) register_8 (
    .D(DATA_IN), .en(demultiplexer_1_out6), .Q(out_11), .clk(register_1_q));  // open: clr
  Register #(.width(16)) register_9 (
    .D(DATA_IN), .en(demultiplexer_1_out7), .Q(out_12), .clk(register_1_q));  // open: clr
  Register #(.width(16)) register_10 (
    .D(DATA_IN), .en(demultiplexer_1_out8), .Q(out_14), .clk(register_1_q));  // open: clr
  Register #(.width(16)) register_11 (
    .D(DATA_IN), .en(demultiplexer_1_out9), .Q(out_15), .clk(register_1_q));  // open: clr
  Register #(.width(16)) register_12 (
    .D(DATA_IN), .en(demultiplexer_1_out10), .Q(out_16), .clk(register_1_q));  // open: clr
  Register #(.width(16)) register_13 (
    .D(DATA_IN), .en(demultiplexer_1_out11), .Q(out_17), .clk(register_1_q));  // open: clr
  Register #(.width(16)) register_14 (
    .D(DATA_IN), .en(demultiplexer_1_out12), .Q(out_18), .clk(register_1_q));  // open: clr
  Register #(.width(16)) register_15 (
    .D(DATA_IN), .en(demultiplexer_1_out13), .Q(out_19), .clk(register_1_q));  // open: clr
  Register #(.width(16)) register_16 (
    .D(DATA_IN), .en(demultiplexer_1_out14), .Q(out_20), .clk(register_1_q));  // open: clr
  Register #(.width(16)) register_17 (
    .D(DATA_IN), .en(demultiplexer_1_out15), .Q(out_21), .clk(register_1_q));  // open: clr
  Multiplexer #(.select(4), .width(16), .enable("false")) multiplexer_1 (
    .in0(out_5), .in1(out_6), .in2(out_7), .in3(out_8), .in4(out_9), .in5(out_10), .in6(out_11),
    .in7(out_12), .in8(out_14), .in9(out_15), .in10(out_16), .in11(out_17), .in12(out_18), .in13(out_19),
    .in14(out_20), .in15(out_21), .out(DATA_OUT), .sel(ADR));
endmodule

module MEMTTY (
  input  EN,
  input  WE,
  input  [15:0] VALIN,
  input  [1:0] ADR,
  output CLOCK,
  output WTENABLE,
  output CLEAR,
  output [6:0] CHAR,
  output [15:0] MEMOUT
);

  wire and_1_out, clock_1_out, clock_2_out, demultiplexer_1_out0, demultiplexer_1_out1, demultiplexer_1_out2,
       register_1_q;
  wire [15:1] register_2_q, register_3_q;
  wire [15:7] register_4_q;

  and and_1 (and_1_out, EN, WE);
  Demultiplexer #(.select(2), .enable("false")) demultiplexer_1 (
    .out0(demultiplexer_1_out0), .out1(demultiplexer_1_out1), .out2(demultiplexer_1_out2), .in(and_1_out),
    .sel(ADR));  // open: out3
  Register #(.width(1)) register_1 (.D(demultiplexer_1_out2), .Q(register_1_q), .clk(clock_1_out));  // open: en, clr
  Register #(.width(16)) register_2 (
    .D(VALIN), .en(demultiplexer_1_out0), .Q({register_2_q, WTENABLE}), .clk(clock_2_out));  // open: clr
  Register #(.width(16)) register_3 (
    .D(VALIN), .en(demultiplexer_1_out1), .Q({register_3_q, CLEAR}), .clk(clock_2_out));  // open: clr
  Register #(.width(16)) register_4 (
    .D(VALIN), .en(demultiplexer_1_out2), .Q({register_4_q, CHAR}), .clk(clock_2_out));  // open: clr
  Multiplexer #(.select(2), .width(16), .enable("false")) multiplexer_1 (
    .in0({register_2_q, WTENABLE}), .in1({register_3_q, CLEAR}), .in2({register_4_q, CHAR}),
    .in3({register_4_q, CHAR}), .out(MEMOUT), .sel(ADR));
  Register #(.width(1), .trigger("falling")) register_5 (
    .D(register_1_q), .Q(CLOCK), .clk(clock_1_out));  // open: en, clr
  Clock clock_1 (.out(clock_1_out));
  Clock clock_2 (.out(clock_2_out));
endmodule

module MEMJOY (
  input  [3:0] ABS_JOY,
  input  [3:0] ORD_JOY,
  input  ADR,
  output [15:0] out_4
);

  wire clock_1_out;
  wire [3:0] register_1_q, register_2_q;

  Clock clock_1 (.out(clock_1_out));
  Register #(.width(4)) register_1 (.D(ABS_JOY), .Q(register_1_q), .clk(clock_1_out));  // open: en, clr
  Register #(.width(4)) register_2 (.D(ORD_JOY), .Q(register_2_q), .clk(clock_1_out));  // open: en, clr
  Multiplexer #(.width(4), .enable("false")) multiplexer_1 (
    .in0(register_1_q), .in1(register_2_q), .out(out_4[3:0]), .sel(ADR));

  assign out_4[15:4] = {12{1'b0}};
endmodule
