// Logisim project ProcoLP.circ as structural Verilog
module IF (
  input  [15:0] PC,
  output [15:0] INS,
  output [15:0] PC_2,
  output [15:0] PC_1
);

  ROM #(.addrWidth(16), .dataWidth(16)) rom_1 (.addr(PC), .data(INS), .sel(1'b1));
  Adder #(.width(16)) adder_1 (.a(PC), .b(16'h1), .out(PC_1));  // open: cin, cout

  assign PC_2 = PC;

  // Notes on the sheet:
  //   contents of rom_1 (hex, n*v repeats v):
  //   0 f
endmodule

module ID (
  input  [15:0] PC_in,
  input  [15:0] INS,
  input  [2:0] TGT_sel,
  input  [15:0] TGT,
  input  WE,
  output [15:0] PC_out,
  output [2:0] OP,
  output [2:0] rT,
  output [15:0] SRC1,
  output [15:0] SRC2,
  output [15:0] ope0
);

  wire ctl6_1_op0, ctl6_1_s2;
  wire [2:0] multiplexer_1_out;
  wire [15:0] left_shift_6_1_out, sign_ext_7_1_out;

  Sign_Ext_7 sign_ext_7_1 (.in(INS[15:6]), .out(sign_ext_7_1_out));
  Left_shift_6 left_shift_6_1 (.in(INS[15:6]), .out(left_shift_6_1_out));
  CTL7 ctl7_1 (.OP_in(INS[2:0]), .rA(INS[5:3]), .OP_out(OP), .rT(rT));
  CTL6 ctl6_1 (.OP(OP), .s2(ctl6_1_s2), .op0(ctl6_1_op0));
  Multiplexer #(.width(3), .enable("false")) multiplexer_1 (
    .in0(INS[5:3]), .in1(INS[15:13]), .out(multiplexer_1_out), .sel(ctl6_1_s2));
  Multiplexer #(.width(16), .enable("false")) multiplexer_2 (
    .in0(sign_ext_7_1_out), .in1(left_shift_6_1_out), .out(ope0), .sel(ctl6_1_op0));
  RegisterFile registerfile_1 (
    .SRC1_in(INS[8:6]), .WE(WE), .SRC2_in(multiplexer_1_out), .TGT_sel(TGT_sel), .TGT_in(TGT),
    .SRC1_out(SRC1), .SRC2_out(SRC2));

  assign PC_out = PC_in;
endmodule

module RegisterFile (
  input  [2:0] TGT_sel,
  input  [15:0] TGT_in,
  input  [2:0] SRC1_in,
  input  WE,
  input  [2:0] SRC2_in,
  output [15:0] SRC1_out,
  output [15:0] SRC2_out
);

  wire demultiplexer_1_out1, demultiplexer_1_out2, demultiplexer_1_out3, demultiplexer_1_out4,
       demultiplexer_1_out5, demultiplexer_1_out6, demultiplexer_1_out7;
  wire [15:0] demultiplexer_2_out1, demultiplexer_2_out2, demultiplexer_2_out3, demultiplexer_2_out4,
       demultiplexer_2_out5, demultiplexer_2_out6, demultiplexer_2_out7, register_1_q, register_2_q,
       register_3_q, register_4_q, register_5_q, register_6_q, register_7_q, register_8_q;

  Demultiplexer #(.select(3)) demultiplexer_1 (
    .out1(demultiplexer_1_out1), .out2(demultiplexer_1_out2), .out3(demultiplexer_1_out3),
    .out4(demultiplexer_1_out4), .out5(demultiplexer_1_out5), .out6(demultiplexer_1_out6),
    .out7(demultiplexer_1_out7), .in(WE), .sel(TGT_sel));  // open: out0, en
  Register #(.width(16), .trigger("high")) register_1 (.D({16{1'b0}}), .Q(register_1_q));  // open: en, clk, clr
  Demultiplexer #(.select(3), .width(16)) demultiplexer_2 (
    .out1(demultiplexer_2_out1), .out2(demultiplexer_2_out2), .out3(demultiplexer_2_out3),
    .out4(demultiplexer_2_out4), .out5(demultiplexer_2_out5), .out6(demultiplexer_2_out6),
    .out7(demultiplexer_2_out7), .in(TGT_in), .sel(TGT_sel));  // open: out0, en
  Register #(.width(16), .trigger("high")) register_2 (
    .D(demultiplexer_2_out1), .Q(register_2_q), .clk(demultiplexer_1_out1));  // open: en, clr
  Register #(.width(16), .trigger("high")) register_3 (
    .D(demultiplexer_2_out2), .Q(register_3_q), .clk(demultiplexer_1_out2));  // open: en, clr
  Register #(.width(16), .trigger("high")) register_4 (
    .D(demultiplexer_2_out3), .Q(register_4_q), .clk(demultiplexer_1_out3));  // open: en, clr
  Register #(.width(16), .trigger("high")) register_5 (
    .D(demultiplexer_2_out4), .Q(register_5_q), .clk(demultiplexer_1_out4));  // open: en, clr
  Register #(.width(16), .trigger("high")) register_6 (
    .D(demultiplexer_2_out5), .Q(register_6_q), .clk(demultiplexer_1_out5));  // open: en, clr
  Register #(.width(16), .trigger("high")) register_7 (
    .D(demultiplexer_2_out6), .Q(register_7_q), .clk(demultiplexer_1_out6));  // open: en, clr
  Register #(.width(16), .trigger("high")) register_8 (
    .D(demultiplexer_2_out7), .Q(register_8_q), .clk(demultiplexer_1_out7));  // open: en, clr
  Multiplexer #(.select(3), .width(16)) multiplexer_1 (
    .in0(register_1_q), .in1(register_2_q), .in2(register_3_q), .in3(register_4_q), .in4(register_5_q),
    .in5(register_6_q), .in6(register_7_q), .in7(register_8_q), .out(SRC1_out), .sel(SRC1_in));  // open: en
  Multiplexer #(.select(3), .width(16)) multiplexer_2 (
    .in0(register_1_q), .in1(register_2_q), .in2(register_3_q), .in3(register_4_q), .in4(register_5_q),
    .in5(register_6_q), .in6(register_7_q), .in7(register_8_q), .out(SRC2_out), .sel(SRC2_in));  // open: en
endmodule

module CTL7 (
  input  [2:0] OP_in,
  input  [2:0] rA,
  output [2:0] OP_out,
  output [2:0] rT
);

  wire and_1_out, and_2_out, and_3_out, not_1_out;

  and and_1 (and_1_out, OP_in[2], ~OP_in[1], OP_in[0]);  // AND_Gate
  and and_2 (and_2_out, ~and_1_out, ~and_3_out);  // AND_Gate
  assign rT = and_2_out ? rA : 3'bz;  // Controlled_Buffer controlled_buffer_1
  and and_3 (and_3_out, OP_in[0], OP_in[1], ~OP_in[2]);  // AND_Gate
  not not_1 (not_1_out, and_2_out);
  assign rT = not_1_out ? 3'b000 : 3'bz;  // Controlled_Buffer controlled_buffer_2

  assign OP_out = OP_in;
endmodule

module CTL6 (
  input  [2:0] OP,
  output s2,
  output op0
);

  and and_1 (s2, ~OP[0], ~OP[2]);  // AND_Gate
  nand nand_1 (op0, ~OP[0], OP[1], OP[2]);  // NAND_Gate

  // Notes on the sheet:
  //   0 => rA
  //   1 => RC
  //   1 => Left-Shift 6
endmodule

module Left_shift_6 (
  input  [9:0] in,
  output [15:0] out
);


  assign out = {in, {6{1'b0}}};
endmodule

module Sign_Ext_7 (
  input  [9:0] in,
  output [15:0] out
);


  assign out = {in[6], {9{1'b0}}, in[5:0]};
endmodule
